# Fritzing sketch DataLogging_DHT11 (saved by Fritzing 1.0.4)

parts:
  Part1 = Arduino Uno (Rev3)
  RTC_module = ZS-042 RTC Module
  LED1 = smd LED [color="Red (633nm)" package="0603 [SMD]"]
  R1 = Resistor [tolerance=±5% resistance=220 package="2010 [SMD]"]
  DHT11 = KY-015 Temperature & Humidity Sensor Module [package="Breakout board"]
  microSD1 = MicroSD Card Module [part_number="Sd Card Module"]

nets:
  N1: Part1.A4/SDA, RTC_module.SDA
  N2: Part1.A5/SCL, RTC_module.SCL
  N3: Part1.D10_PWM/SS, microSD1.CS
  N4: Part1.D11_PWM/MOSI, microSD1.MOSI
  N5: Part1.D12/MISO, microSD1.MISO
  N6: Part1.D13/SCK, microSD1.SCK
  GND: Part1.GND, RTC_module.GND, LED1.anode, DHT11.-, microSD1.GND
  N7: Part1.D2, DHT11.S
  N8: Part1.D7, R1.Pin_0
  5V: Part1.5V, DHT11.Vin, microSD1.VCC
  N9: LED1.cathode, R1.Pin_1

notes:
  SD Card wiring
  CS to pin 10
  DI to pin 11
  DO to pin 12
  CLK to pin 13
  GND to GND
  5V to 5V

custom parts:
  KY-015 Temperature & Humidity Sensor Module: KY-015 temperature and humidity sensor module, provides a low-latency serial interface to measure humidity and temperature.
